// Logisim project q6-trigger.circ as structural Verilog: 1 circuit, main circuit main
module main (
  input  Reset,
  input  Preset,
  input  C,
  input  D,
  output Q,
  output nQ
);

  wire _1_out, _2_out, _3_out, _4_out;

  nand _1 (_1_out, _2_out, Preset, _4_out);
  nand _2 (_2_out, _1_out, Reset, C);
  nand _6 (nQ, Q, Reset, _3_out);
  nand _5 (Q, _2_out, Preset, nQ);
  nand _3 (_3_out, _2_out, C, _4_out);
  nand _4 (_4_out, _3_out, Reset, D);
endmodule
